# Fritzing sketch BounceBoard (saved by Fritzing 0.6.3b)
breadboards: 1

parts:
  Arduino1 = Arduino
  J1 = Piezo Speaker
  J2 = Piezo Speaker
  R1 = Resistor [tolerance=±5% resistance=220 package=THT]
  LED1 = LED - 5mm [color="Red (633nm)" package="5 mm [THT]"]

nets:
  N1: Arduino1.GND, J1.pin1, J2.pin1, R1.Pin_1, LED1.cathode
  N2: Arduino1.D13, LED1.anode
  N3: Arduino1.D4, J1.pin2
  N4: Arduino1.A0, J2.pin2, R1.Pin_0
