# Fritzing sketch BounceMaster (saved by Fritzing 0.6.3b)
breadboards: 1

parts:
  Arduino1 = Arduino
  J1 = Piezo Speaker
  J2 = Piezo Speaker
  R1 = Resistor [tolerance=±5% resistance=220 package=THT]
  LED1 = LED - 5mm [color="Red (633nm)" package="5 mm [THT]"]
  VCC1 = Battery

nets:
  N1: Arduino1.GND, J1.pin1, J2.pin1, R1.Pin_1, LED1.cathode, VCC1.-
  N2: Arduino1.D13, LED1.anode
  N3: Arduino1.D3, J1.pin2
  N4: Arduino1.VIN, VCC1.+
  N5: Arduino1.A0, J2.pin2, R1.Pin_0
